// Digital circuit Computer.dig as structural Verilog
module Computer (
  input  C
);

  wire addressdecoder_1_p2, addressdecoder_1_p3, addressdecoder_1_p4, addressdecoder_1_p5,
       addressdecoder_1_p6, cpu_1_halted, cpu_1_nre, cpu_1_nwe;
  wire [31:0] cpu_1_addressbus, cpu_1_databus_out, gpu_1_d_out;

  CPU cpu_1 (
    .Clock(C), .Databus_in(gpu_1_d_out), .Addressbus(cpu_1_addressbus), .Databus_out(cpu_1_databus_out),
    .nRE(cpu_1_nre), .nWE(cpu_1_nwe), .Halted(cpu_1_halted));
  // AddressDecoder addressdecoder_1: pin names not known; wires that end beside it: cpu_1_addressbus, addressdecoder_1_p2, addressdecoder_1_p3, addressdecoder_1_p4, addressdecoder_1_p5, addressdecoder_1_p6
  GPU #(.generic("Height := 48; Width := 64;")) gpu_1 (
    .C(C), .nRE(cpu_1_nre), .nWE(cpu_1_nwe), .D_in(cpu_1_databus_out), .A(cpu_1_addressbus),
    .A_vramctl(addressdecoder_1_p5), .A_vram(addressdecoder_1_p6), .D_out(gpu_1_d_out));
  RAM ram_1 (
    .C(C), .nRE(cpu_1_nre), .nWE(cpu_1_nwe), .D_in(cpu_1_databus_out), .A(cpu_1_addressbus),
    .A_ram(addressdecoder_1_p2), .D_out(gpu_1_d_out));
  DevInfo #(.generic("clockrate := 50000;")) devinfo_1 (
    .C(C), .nRE(cpu_1_nre), .A(cpu_1_addressbus), .A_dev(addressdecoder_1_p4), .D_out(gpu_1_d_out));
  Terminal #(.generic("LineWidth := 80; Lines := 24;")) terminal_1 (
    .C(C), .nRE(cpu_1_nre), .nWE(cpu_1_nwe), .D_in(cpu_1_databus_out), .A(cpu_1_addressbus),
    .A_io(addressdecoder_1_p3), .D_out(gpu_1_d_out));
  Break break_1 (.brk(cpu_1_halted));
  Stop stop_1 (.stop(cpu_1_halted));
  // Probe halted on cpu_1_halted
  // Probe nRE on cpu_1_nre
  // Probe nWE on cpu_1_nwe
  // Probe databusToCPU on gpu_1_d_out
  // Probe databusFromCPU on cpu_1_databus_out
  // Probe addressbus on cpu_1_addressbus
  // Probe address_ram on addressdecoder_1_p2
  // Probe address_io on addressdecoder_1_p3
  // Probe address_dev on addressdecoder_1_p4
  // Probe address_vramctl on addressdecoder_1_p5
  // Probe address_vram on addressdecoder_1_p6

  // Notes on the sheet:
  //   C: Hz: 50000
  //   Original Hades design by David N. Jansen, Radboud Universiteit Nijmegen, Nederland (2012)
  //   Ported to Digital and modified by Ciske Harsema (2019+2020)
endmodule
