// Digital circuit DevInfo.dig as structural Verilog
// A device that can be queried to obtain some information about the device, such as timing information. The device keeps track of a timestamp, which is incremented on each rising clock edge.
module DevInfo (
  input  C,
  input  nRE,
  input  [31:0] A,
  input  A_dev,
  output [31:0] D_out
);

  wire and_1_out;
  wire [31:0] multiplexer_1_out, TS_out;

  Counter #(.Bits(32)) TS (.en(1'b1), .C(C), .clr(1'b0), .out(TS_out));  // open: ovf
  Multiplexer #(.Selector_Bits(2), .Bits(32)) multiplexer_1 (
    .sel(A[3:2]), .in_0(TS_out), .in_1(32'hc350), .in_2(32'h32), .in_3(32'h4447544c), .out(multiplexer_1_out));
  and and_1 (and_1_out, ~nRE, A_dev);  // And
  assign D_out = and_1_out ? multiplexer_1_out : 32'bz;  // Driver driver_1

  // Notes on the sheet:
  //   nRE: Active low read enabled input. A low value indicates a read operation should be performed.
  //   D_out: Data output, containing the data that was read during a read operation. If no read operation occured it is in a high z state.
  //   A: Address input, which indicates what address to read from or write to.
  //   A_dev: Device information address input, which indicates wheter the address belongs to the device information address range.
endmodule
