// Digital circuit GPU.dig as structural Verilog
// A basic GPU device, which contains a dubble buffered VRAM that can be rendered to a screen. Only one buffer is active at a time, and the screen is redrawn once the buffer is swapped.
module GPU (
  input  C,
  input  nRE,
  input  nWE,
  input  [31:0] D_in,
  input  [31:0] A,
  input  A_vramctl,
  input  A_vram,
  output [31:0] D_out
);

  wire and_1_out, and_2_out, and_3_out, and_4_out, and_5_out, and_6_out, multiplexer_1_out, nand_1_out,
       not_1_out, not_2_out;
  wire [0:0] BUF_q;
  wire [12:0] add_1_s, multiplexer_3_out;
  wire [15:0] VRAM_d;
  wire [31:0] multiplexer_2_out;

  nand nand_1 (nand_1_out, A[2], A[3]);
  and and_1 (and_1_out, ~nWE, A_vramctl, nand_1_out);  // And
  not not_1 (not_1_out, BUF_q[0]);
  Multiplexer multiplexer_1 (.sel(D_in[0]), .in_0(not_1_out), .in_1(D_in[1]), .out(multiplexer_1_out));
  Register BUF (.D(multiplexer_1_out), .C(C), .en(and_1_out), .Q(BUF_q[0]));
  Multiplexer #(.Selector_Bits(2), .Bits(32)) multiplexer_2 (
    .sel(A[3:2]), .in_0({{31{1'b0}}, BUF_q[0]}), .in_1(32'h40), .in_2(32'h30), .in_3(32'h1),
    .out(multiplexer_2_out));
  and and_2 (and_2_out, ~nRE, A_vramctl);  // And
  assign D_out = and_2_out ? multiplexer_2_out : 32'bz;  // Driver driver_1
  Add #(.Bits(13), .generic("this.Bits = bitsNeededFor(args.Width * args.Height * 2);")) add_1 (
    .a(A[14:2]), .b(13'hc00), .c_i(1'b0), .s(add_1_s));  // open: c_o
  Multiplexer #(.Bits(13), .generic("this.Bits = bitsNeededFor(args.Width * args.Height * 2);")) multiplexer_3 (
    .sel(not_2_out), .in_0(A[14:2]), .in_1(add_1_s), .out(multiplexer_3_out));
  not not_2 (not_2_out, BUF_q[0]);
  and and_3 (and_3_out, A_vram, ~nWE);  // And
  and and_4 (and_4_out, A_vram, ~nRE);  // And
  GraphicCard #(.graphicHeight(48), .graphicWidth(64), .Bits(16), .generic("this.graphicWidth = args.Width; this.graphicHeight = args.Height;")) VRAM (
    .A(multiplexer_3_out), .str(and_3_out), .C(C), .ld(and_4_out), .B(BUF_q[0]), .D(VRAM_d));
  assign VRAM_d = and_5_out ? D_in[15:0] : 16'bz;  // Driver driver_2
  and and_5 (and_5_out, ~nWE, A_vram);  // And
  and and_6 (and_6_out, ~nRE, A_vram);  // And
  assign D_out = and_6_out ? {{16{1'b0}}, VRAM_d} : 32'bz;  // Driver driver_3

  // Notes on the sheet:
  //   nRE: Active low read enabled input. A low value indicates a read operation should be performed.
  //   nWE: Active low write enabled input. A low value indicates a write operation should be performed.
  //   D_in: Data input, containing the data to be written during a write operation.
  //   D_out: Data output, containing the data that was read during a read operation. If no read operation occured it is in a high z state.
  //   A: Address input, which indicates what address to read from or write to.
  //   A_vramctl: VRAM control address input, which indicates wheter the address belongs to the VRAM control address range.
  //   A_vram: VRAM address input, which indicates wheter the address belongs to the VRAM address range.
  //   b = w * h
  //   (offset to second buffer)
endmodule
