// Digital circuit RAM.dig as structural Verilog
// A simple 256KiB RAM device. This device contains the program memory, which will be initialized with the contents of an assembled program if Digital is configured to preload the program memory at startup.
module RAM (
  input  C,
  input  nRE,
  input  nWE,
  input  [31:0] D_in,
  input  [31:0] A,
  input  A_ram,
  output [31:0] D_out
);

  wire and_1_out, and_2_out;

  and and_1 (and_1_out, ~nWE, A_ram);  // And
  and and_2 (and_2_out, A_ram, ~nRE);  // And
  RAMDualPort #(.AddrBits(18), .isProgramMemory("true"), .Bits(32)) RAM (
    .A(A[19:2]), .Din(D_in), .str(and_1_out), .C(C), .ld(and_2_out), .D(D_out));

  // Notes on the sheet:
  //   D_out: Data output, containing the data that was read during a read operation. If no read operation occured it is in a high z state.
  //   nRE: Active low read enabled input. A low value indicates a read operation should be performed.
  //   nWE: Active low write enabled input. A low value indicates a write operation should be performed.
  //   D_in: Data input, containing the data to be written during a write operation.
  //   A: Address input, which indicates what address to read from or write to.
  //   A_ram: RAM address input, which indicates wheter the address belongs to the RAM address range.
endmodule
