// Digital circuit Terminal.dig as structural Verilog
// A terminal device, which allows reading characters from a keyboard and writing characters to a terminal window.
module Terminal (
  input  C,
  input  nRE,
  input  nWE,
  input  [31:0] D_in,
  input  [31:0] A,
  input  A_io,
  output [31:0] D_out
);

  wire and_1_out, and_2_out, and_3_out, and_4_out;
  wire [0:0] keyboard_1_av;
  wire [15:0] keyboard_1_d;
  wire [31:0] multiplexer_1_out;

  and and_1 (and_1_out, A_io, ~A[3], ~A[2]);  // And
  Terminal #(.generic("this.termWidth = args.LineWidth; this.termHeight = args.Lines;")) terminal_1 (
    .D(D_in), .C(C), .en(and_2_out));
  and and_2 (and_2_out, ~nWE, and_1_out);  // And
  and and_3 (and_3_out, ~nRE, and_1_out);  // And
  Keyboard keyboard_1 (.C(C), .en(and_3_out), .D(keyboard_1_d), .av(keyboard_1_av[0]));
  and and_4 (and_4_out, ~nRE, A_io);  // And
  Multiplexer #(.Selector_Bits(2), .Bits(32)) multiplexer_1 (
    .sel(A[3:2]), .in_0({{16{1'b0}}, keyboard_1_d}), .in_1({{31{1'b0}}, keyboard_1_av[0]}), .in_2(32'h32),
    .in_3(32'h19), .out(multiplexer_1_out));
  assign D_out = and_4_out ? multiplexer_1_out : 32'bz;  // Driver driver_1

  // Notes on the sheet:
  //   nRE: Active low read enabled input. A low value indicates a read operation should be performed.
  //   nWE: Active low write enabled input. A low value indicates a write operation should be performed.
  //   D_out: Data output, containing the data that was read during a read operation. If no read operation occured it is in a high z state.
  //   D_in: Data input, containing the data to be written during a write operation.
  //   A: Address input, which indicates what address to read from or write to.
  //   A_io: IO address input, which indicates wheter the address belongs to the IO address range.
endmodule
