// Digital circuit ALU.dig as structural Verilog
// The Arithmetic Logic Unit (ALU) component, which can perform various operations on the provided operands, also determining the resulting flag values.
module ALU (
  input  [31:0] B,
  input  [31:0] A,
  input  [2:0] Opcode,
  output [31:0] Result,
  output Carry,
  output Overflow,
  output Negative,
  output Zero
);

  wire add_1_c_o, and_3_out, and_4_out, and_5_out, and_6_out, not_2_out, not_3_out, not_4_out, not_5_out,
       not_6_out, not_7_out, not_8_out, or_2_out, or_3_out, sub_1_c_o, xor_2_out;
  wire [31:0] add_1_s, and_1_out, and_2_out, not_1_out, or_1_out, Rotator_out, sub_1_s, xor_1_out;

  assign not_1_out = ~B;  // Not not_1, 32 bits wide
  assign or_1_out = A | B;  // Or or_1, 32 bits wide
  assign xor_1_out = A ^ B;  // XOr xor_1, 32 bits wide
  assign and_1_out = A & B;  // And and_1, 32 bits wide
  assign and_2_out = A & not_1_out;  // And and_2, 32 bits wide
  BarrelShifter #(.Bits(32), .barrelShifterMode("rotate")) Rotator (.in(B), .shift(A[5:0]), .out(Rotator_out));
  Add #(.Bits(32)) add_1 (.a(A), .b(B), .c_i(1'b0), .s(add_1_s), .c_o(add_1_c_o));
  Sub #(.Bits(32)) sub_1 (.a(A), .b(B), .c_i(1'b0), .s(sub_1_s), .c_o(sub_1_c_o));
  not not_2 (not_2_out, A[31]);
  not not_3 (not_3_out, B[31]);
  not not_4 (not_4_out, add_1_s[31]);
  not not_5 (not_5_out, A[31]);
  not not_6 (not_6_out, B[31]);
  not not_7 (not_7_out, sub_1_s[31]);
  not not_8 (not_8_out, sub_1_c_o);
  and and_3 (and_3_out, not_2_out, not_3_out, add_1_s[31]);
  and and_4 (and_4_out, A[31], B[31], not_4_out);
  and and_5 (and_5_out, not_5_out, B[31], sub_1_s[31]);
  and and_6 (and_6_out, A[31], not_6_out, not_7_out);
  Multiplexer #(.Selector_Bits(3), .Bits(32)) multiplexer_1 (
    .sel(Opcode), .in_0(or_1_out), .in_1(xor_1_out), .in_2(and_1_out), .in_3(and_2_out), .in_4({32{1'b0}}),
    .in_5(Rotator_out), .in_6(add_1_s), .in_7(sub_1_s), .out({Negative, Result[30:0]}));
  Multiplexer #(.Selector_Bits(3)) multiplexer_2 (
    .sel(Opcode), .in_0(1'b0), .in_1(1'b0), .in_2(1'b0), .in_3(1'b0), .in_4(1'b0), .in_5(Rotator_out[0]),
    .in_6(add_1_c_o), .in_7(not_8_out), .out(Carry));
  xor xor_2 (xor_2_out, Rotator_out[31], B[31]);
  or or_2 (or_2_out, and_3_out, and_4_out);
  or or_3 (or_3_out, and_5_out, and_6_out);
  Multiplexer #(.Selector_Bits(3)) multiplexer_3 (
    .sel(Opcode), .in_0(1'b0), .in_1(1'b0), .in_2(1'b0), .in_3(1'b0), .in_4(1'b0), .in_5(xor_2_out),
    .in_6(or_2_out), .in_7(or_3_out), .out(Overflow));
  All32Bits0 all32bits0_1 (.Input({Negative, Result[30:0]}), .All32Bits0(Zero));

  assign Result[31] = Negative;

  // Notes on the sheet:
  //   B: The value of the ALU B operand.
  //   A: The value of the ALU A operand.
  //   Result: The resuling value, containing the value computed by the ALU.
  //   Carry: The resulting carry flag.
  //   Overflow: The resulting overflow flag.
  //   Negative: The resulting negative flag.
  //   Zero: The resulting zero flag.
  //   Opcode: The ALU opcode, which specifies the operation to perform.
endmodule

/* Test case:
A B Opcode Result Carry Overflow Negative Zero

loop(i, 256)
    # determine random values for A and B inputs
    let a = random(1<<32);
    let b = random(1<<32);

    # compute expected Result
    let rot = a & 31;
    let r = (b << rot) | (b >> (32-rot));

    # determine expected flags
    let c = r & 1;
    let o = ((b>>31) & 1) != ((r>>31) & 1);
    let n = (r>>31) & 1;
    let z = r=0;

    # perform rotation, and then check Result and flags are as expected
    (a) (b) 5 (r) (c) (o) (n) (z)
end loop
*/

/* Test case:
A B Opcode Result Carry Overflow Negative Zero

loop(i, 256)
    # determine random values for A and B inputs
    let a = random(1<<32);
    let b = random(1<<32);

    # compute expected Result
    let r = a + (~b & 0xffffffff) + 1;

    # determine expected flags
    let c = (r) >= (1<<32);
    let o = (((a>>31) & 1) != ((b>>31) & 1)) & (((a>>31) & 1) != ((r>>31) & 1));
    let n = (r>>31) & 1;
    let z = r=0;

    # perform subtraction, and then check Result and flags are as expected
    (a) (b) 7 (r) (c) (o) (n) (z)
end loop
*/
