// Digital circuit All32Bits0.dig as structural Verilog
module All32Bits0 (
  input  [31:0] Input,
  output All32Bits0
);

  wire [31:0] not_1_out;

  assign not_1_out = ~Input;  // Not not_1, 32 bits wide
  and and_1 (All32Bits0, not_1_out[0], not_1_out[1], not_1_out[2], not_1_out[3], not_1_out[4], not_1_out[5], not_1_out[6], not_1_out[7], not_1_out[8], not_1_out[9], not_1_out[10], not_1_out[11], not_1_out[12], not_1_out[13], not_1_out[14], not_1_out[15], not_1_out[16], not_1_out[17], not_1_out[18], not_1_out[19], not_1_out[20], not_1_out[21], not_1_out[22], not_1_out[23], not_1_out[24], not_1_out[25], not_1_out[26], not_1_out[27], not_1_out[28], not_1_out[29], not_1_out[30], not_1_out[31]);
endmodule
