// Digital circuit All6Bits1.dig as structural Verilog
module All6Bits1 (
  input  [5:0] XNorOutput,
  output All6Bits1
);

  and and_1 (All6Bits1, XNorOutput[0], XNorOutput[1], XNorOutput[2], XNorOutput[3], XNorOutput[4], XNorOutput[5]);
endmodule
