// Digital circuit AllBits1.dig as structural Verilog
module AllBits1 (
  input  [27:0] Instruction_NoCond,
  output AllBits1
);

  and and_1 (AllBits1, Instruction_NoCond[0], Instruction_NoCond[1], Instruction_NoCond[2], Instruction_NoCond[3], Instruction_NoCond[4], Instruction_NoCond[5], Instruction_NoCond[6], Instruction_NoCond[7], Instruction_NoCond[8], Instruction_NoCond[9], Instruction_NoCond[10], Instruction_NoCond[11], Instruction_NoCond[12], Instruction_NoCond[13], Instruction_NoCond[14], Instruction_NoCond[15], Instruction_NoCond[16], Instruction_NoCond[17], Instruction_NoCond[18], Instruction_NoCond[19], Instruction_NoCond[20], Instruction_NoCond[21], Instruction_NoCond[22], Instruction_NoCond[23], Instruction_NoCond[24], Instruction_NoCond[25], Instruction_NoCond[26], Instruction_NoCond[27]);
endmodule
