// Digital circuit InstructionDecoder.dig as structural Verilog
// The InstructionDecoder component, which serves as a hub to control many of the signals to other components. It implements both the fetch operation, and execution of machine code (including decoding).
module InstructionDecoder (
  input  [31:0] Instruction,
  input  Fetch,
  input  Execute,
  input  [31:0] SP,
  input  Clock,
  input  [31:0] PC,
  output [3:0] Condition,
  output [3:0] Reg_B,
  output [3:0] Reg_A,
  output [2:0] Opcode,
  output nWE,
  output [31:0] Constant,
  output SetFlags,
  output UseConstant,
  output PUSH,
  output POP,
  output LOADHI,
  output ARITHMETIC,
  output [2:0] _31bitnREnWE,
  output [31:0] SPafterPUSH,
  output [31:0] PCafterFETCH,
  output nRE,
  output Halt,
  output [3:0] Reg_dest
);

  wire all6bits1_1_all6bits1, all6bits1_2_all6bits1, all6bits1_3_all6bits1, all6bits1_4_all6bits1,
       all6bits1_5_all6bits1, and_1_out, multiplexer_7_out, multiplexer_10_out, not_1_out, not_6_out,
       or_4_out;
  wire [0:0] or_1_out;
  wire [1:0] xnor_1_out;
  wire [2:1] not_2_out;
  wire [3:0] multiplexer_9_out, multiplexer_13_out;
  wire [5:0] or_2_out, xnor_2_out, xnor_3_out, xnor_4_out, xnor_5_out;
  wire [31:0] add_1_s, add_2_s, barrelshifter_1_out, bitextender_1_out, bitextender_2_out, Instruction_q,
       multiplexer_3_out;

  Register #(.Bits(32)) u_Instruction (
    .D(Instruction), .C(Clock), .en(Fetch),
    .Q({Instruction_q[31:28], SetFlags, Instruction_q[26:16], Reg_A, Instruction_q[11:0]}));
  assign xnor_1_out = ~(2'b01 ^ Instruction_q[31:30]);  // XNOr xnor_1, 2 bits wide
  assign xnor_2_out = ~(6'b110100 ^ {Instruction_q[31:28], SetFlags, Instruction_q[26]});  // XNOr xnor_2, 6 bits wide
  assign xnor_3_out = ~(6'b110001 ^ {Instruction_q[31:28], SetFlags, Instruction_q[26]});  // XNOr xnor_3, 6 bits wide
  assign xnor_4_out = ~(6'b111000 ^ {Instruction_q[31:28], SetFlags, Instruction_q[26]});  // XNOr xnor_4, 6 bits wide
  assign xnor_5_out = ~(6'b110000 ^ {Instruction_q[31:28], SetFlags, Instruction_q[26]});  // XNOr xnor_5, 6 bits wide
  and and_1 (and_1_out, xnor_1_out[0], xnor_1_out[1]);
  All6Bits1 all6bits1_1 (.XNorOutput(xnor_2_out), .All6Bits1(all6bits1_1_all6bits1));
  All6Bits1 all6bits1_2 (.XNorOutput(xnor_5_out), .All6Bits1(all6bits1_2_all6bits1));
  All6Bits1 all6bits1_3 (.XNorOutput(xnor_4_out), .All6Bits1(all6bits1_3_all6bits1));
  or or_1 (or_1_out[0], all6bits1_1_all6bits1, Fetch, all6bits1_2_all6bits1);
  assign or_2_out = xnor_3_out | xnor_4_out;  // Or or_2, 6 bits wide
  AllBits1 allbits1_1 (
    .Instruction_NoCond({Instruction_q[31:28], SetFlags, Instruction_q[26:16], Reg_A, Instruction_q[11:4]}),
    .AllBits1(Halt));
  All6Bits1 all6bits1_4 (.XNorOutput(xnor_3_out), .All6Bits1(all6bits1_4_all6bits1));
  All6Bits1 all6bits1_5 (.XNorOutput(or_2_out), .All6Bits1(all6bits1_5_all6bits1));
  not not_1 (not_1_out, Instruction_q[26]);
  BitExtender #(.inputBits(10), .outputBits(32)) bitextender_1 (.in(Instruction_q[25:16]), .out(bitextender_1_out));
  Multiplexer #(.Bits(3)) multiplexer_1 (.sel(LOADHI), .in_0(Instruction_q[30:28]), .in_1(3'b110), .out(Opcode));
  not not_2 (not_2_out[1], or_1_out[0]);
  or or_3 (UseConstant, not_1_out, or_1_out[0], all6bits1_3_all6bits1, LOADHI);
  not not_3 (not_2_out[2], all6bits1_3_all6bits1);
  BitExtender #(.inputBits(22), .outputBits(32)) bitextender_2 (
    .in({Instruction_q[29:28], SetFlags, Instruction_q[26:16], Reg_A, Instruction_q[11:8]}),
    .out(bitextender_2_out));
  Add #(.Bits(32)) add_1 (.a(32'hfffffffc), .b(SP), .c_i(1'b0), .s(add_1_s));  // open: c_o
  Multiplexer #(.Bits(32)) multiplexer_2 (.sel(all6bits1_4_all6bits1), .in_0(SP), .in_1(add_1_s), .out(SPafterPUSH));
  Multiplexer #(.Selector_Bits(2), .Bits(32)) multiplexer_3 (
    .sel(Instruction_q[31:30]), .in_0(bitextender_1_out), .in_1(bitextender_1_out), .in_2(bitextender_2_out),
    .in_3(bitextender_1_out), .out(multiplexer_3_out));
  Add #(.Bits(32)) add_2 (.a(32'h4), .b(PC), .c_i(1'b0), .s(add_2_s));  // open: c_o
  Multiplexer #(.Bits(32)) multiplexer_4 (.sel(Fetch), .in_0(PC), .in_1(add_2_s), .out(PCafterFETCH));
  Multiplexer multiplexer_5 (.sel(Execute), .in_0(1'b0), .in_1(and_1_out), .out(LOADHI));
  Multiplexer multiplexer_6 (.sel(Execute), .in_0(1'b0), .in_1(all6bits1_4_all6bits1), .out(PUSH));
  Multiplexer multiplexer_7 (.sel(Execute), .in_0(1'b0), .in_1(all6bits1_5_all6bits1), .out(multiplexer_7_out));
  not not_4 (nWE, multiplexer_7_out);
  not not_5 (nRE, or_1_out[0]);
  Multiplexer #(.Bits(4)) multiplexer_8 (.sel(Halt), .in_0(Instruction_q[3:0]), .in_1(4'b0000), .out(Condition));
  Multiplexer #(.Selector_Bits(2), .Bits(4)) multiplexer_9 (
    .sel({Fetch, or_1_out[0]}), .in_0(Instruction_q[11:8]), .in_1(4'b1110), .in_2(4'b1111), .in_3(4'b0000),
    .out(multiplexer_9_out));
  Multiplexer multiplexer_10 (.sel(Fetch), .in_0(1'b0), .in_1(not_6_out), .out(multiplexer_10_out));
  not not_6 (not_6_out, Instruction_q[31]);
  Multiplexer multiplexer_11 (.sel(Execute), .in_0(1'b0), .in_1(all6bits1_1_all6bits1), .out(POP));
  Multiplexer #(.Bits(3)) multiplexer_12 (
    .sel(Execute), .in_0(3'b000), .in_1({not_2_out, Instruction_q[31]}), .out(_31bitnREnWE));
  Multiplexer #(.Selector_Bits(2), .Bits(4)) multiplexer_13 (
    .sel({Fetch, or_1_out[0]}), .in_0(Instruction_q[7:4]), .in_1(4'b1110), .in_2(4'b1111), .in_3(4'b0000),
    .out(multiplexer_13_out));
  Multiplexer #(.Bits(4)) multiplexer_14 (
    .sel(LOADHI), .in_0(multiplexer_9_out), .in_1(Instruction_q[7:4]), .out(Reg_B));
  Register UseArithmeticIfInExecute (.D(multiplexer_10_out), .C(Clock), .en(Fetch), .Q(ARITHMETIC));
  BarrelShifter #(.Bits(32)) barrelshifter_1 (.in(multiplexer_3_out), .shift(6'b001010), .out(barrelshifter_1_out));
  or or_4 (or_4_out, Fetch, Execute);
  Multiplexer #(.Bits(32)) multiplexer_15 (
    .sel(LOADHI), .in_0(multiplexer_3_out), .in_1(barrelshifter_1_out), .out(Constant));
  Register #(.Bits(4)) UseRegDestIfInFetchOrExecute (.D(multiplexer_13_out), .C(Clock), .en(or_4_out), .Q(Reg_dest));

  // Notes on the sheet:
  //   Instruction: The instruction machine code input. If the CPU is in the fetch phase and a rising clock signal occurs, this machine code is stored in the internal instruction register (IR), so that it can be decoded and executed.
  //   Condition: Instruction condition output, which contains the condition under which the instruction should be executed.
  //   Reg_B: B register output, which determines the register to be used for the second operand.
  //   Reg_A: A register output, which determines the register to be used for the first operand.
  //   Opcode: Opcode output, which determines the operation the ALU should perform.
  //   Reg_dest: Destination register output, which determines the register that should store the result of a data operation. A data operation is either an ALU computation, or a read from an external device, such as RAM.
endmodule
