// Digital circuit InstructionLOADHI.dig as structural Verilog
module InstructionLOADHI (
  input  [31:0] Instruction,
  output [21:0] Constant,
  output [3:0] Reg_dest
);

  // Pins of 1 and 4 bits meet at Instruction[7:4]

  assign Constant = Instruction[29:8];
  assign Reg_dest = Instruction[7:4];
endmodule
