// Digital circuit InstructionREAD.dig as structural Verilog
module InstructionREAD (
  input  [31:0] Instruction,
  output [3:0] Reg_dest,
  output [3:0] Reg_B,
  output [9:0] Constant
);


  assign Constant = Instruction[25:16];
  assign Reg_B = Instruction[11:8];
  assign Reg_dest = Instruction[7:4];
endmodule
