// Digital circuit InstructionSplitter.dig as structural Verilog
module InstructionSplitter (
  input  [31:0] Instruction,
  output [2:0] Opcode,
  output SetFlags,
  output [9:0] Constant,
  output [3:0] Reg_A,
  output [3:0] Reg_B,
  output [3:0] Reg_dest,
  output UseConstant
);

  Multiplexer #(.Bits(10)) multiplexer_1 (
    .sel(Instruction[26]), .in_0(Instruction[25:16]), .in_1({10{1'b0}}), .out(Constant));
  Multiplexer #(.Bits(4)) multiplexer_2 (.sel(Instruction[26]), .in_0(4'b0000), .in_1(Instruction[15:12]), .out(Reg_A));

  assign Opcode = Instruction[30:28];
  assign Reg_B = Instruction[11:8];
  assign Reg_dest = Instruction[7:4];
  assign SetFlags = Instruction[27];
  assign UseConstant = Instruction[26];
endmodule
