// Digital circuit InstructionWRITE.dig as structural Verilog
module InstructionWRITE (
  input  [31:0] Instruction,
  output [3:0] Reg_B,
  output [3:0] Reg_A,
  output [9:0] Constant
);


  assign Constant = Instruction[25:16];
  assign Reg_A = Instruction[15:12];
  assign Reg_B = Instruction[11:8];
endmodule
