// Digital circuit Tester.dig as structural Verilog
// The Tester component, which given a condition and set of flags will test whether the condition was met or not.
module Tester (
  input  [3:0] Condition,
  input  Carry_in,
  input  Overflow_in,
  input  Negative_in,
  input  Zero_in,
  output TestSucceeds
);

  wire and_1_out, and_2_out, not_1_out, not_2_out, not_3_out, not_4_out, not_5_out, not_6_out, not_7_out,
       or_1_out, or_2_out, xnor_1_out, xor_1_out;

  and and_1 (and_1_out, xnor_1_out, not_1_out);
  not not_1 (not_1_out, Zero_in);
  or or_1 (or_1_out, xor_1_out, Zero_in);
  not not_2 (not_2_out, Zero_in);
  not not_3 (not_3_out, Carry_in);
  not not_4 (not_4_out, Negative_in);
  not not_5 (not_5_out, Overflow_in);
  Multiplexer #(.Selector_Bits(4)) multiplexer_1 (
    .sel(Condition), .in_0(Zero_in), .in_1(not_2_out), .in_2(Carry_in), .in_3(not_3_out), .in_4(Negative_in),
    .in_5(not_4_out), .in_6(Overflow_in), .in_7(not_5_out), .in_8(and_2_out), .in_9(or_2_out),
    .in_10(xnor_1_out), .in_11(xor_1_out), .in_12(and_1_out), .in_13(or_1_out), .in_14(1'b0), .in_15(1'b1),
    .out(TestSucceeds));
  not not_6 (not_6_out, Zero_in);
  not not_7 (not_7_out, Carry_in);
  and and_2 (and_2_out, Carry_in, not_6_out);
  or or_2 (or_2_out, Zero_in, not_7_out);
  xnor xnor_1 (xnor_1_out, Negative_in, Overflow_in);
  xor xor_1 (xor_1_out, Negative_in, Overflow_in);

  // Notes on the sheet:
  //   Condition: The condition to test.
  //   TestSucceeds: Determines whether the test succeeded (indicating the instruction should be executed), or failed (indicating the instruction should be skipped).
  //   Carry_in: The input carry flag.
  //   Overflow_in: The input overflow flag.
  //   Negative_in: The input negative flag.
  //   Zero_in: The input zero flag.
endmodule

/* Test case:
Condition Carry_in Overflow_in Negative_in Zero_in TestSucceeds

loop(c, 2)
  loop(o, 2)
    loop(n, 2)
      loop(z, 2)
        0b0100 (c) (o) (n) (z) (n)
        0b1000 (c) (o) (n) (z) (c & !z)
        0b1100 (c) (o) (n) (z) ((n = o) & !z)
        0b1101 (c) (o) (n) (z) ((n != o) | z)
        0b1111 (c) (o) (n) (z) 1
      end loop
    end loop
  end loop
end loop
*/
